// Logisim project CPU_Library.circ as structural Verilog
module AND (
  input  [5:0] A5_A0,
  input  [5:0] B5_B0,
  output [5:0] out_3
);

  and _0 (out_3[0], A5_A0[0], B5_B0[0]);
  and _1 (out_3[1], A5_A0[1], B5_B0[1]);
  and _2 (out_3[2], A5_A0[2], B5_B0[2]);
  and _3 (out_3[3], A5_A0[3], B5_B0[3]);
  and _4 (out_3[4], A5_A0[4], B5_B0[4]);
  and _5 (out_3[5], A5_A0[5], B5_B0[5]);

  // Other names for the same wires on the sheet: A0 = A5_A0[0]; A1 = A5_A0[1]; A2 = A5_A0[2]; A3 = A5_A0[3];
  //   A4 = A5_A0[4]; A5 = A5_A0[5]; B0 = B5_B0[0]; B1 = B5_B0[1]; B2 = B5_B0[2]; B3 = B5_B0[3]; B4 = B5_B0[4];
  //   B5 = B5_B0[5]; R0 = out_3[0]; R1 = out_3[1]; R2 = out_3[2]; R3 = out_3[3]; R4 = out_3[4]; R5 = out_3[5]
endmodule

module ROR (
  input  [5:0] A5_A0,
  input  [2:0] Shift_2_0,
  output [5:0] out_3
);

  Multiplexer #(.select(3), .enable("false")) multiplexer_1 (
    .in0(A5_A0[5]), .in1(A5_A0[0]), .in2(A5_A0[1]), .in3(A5_A0[2]), .in4(A5_A0[3]), .in5(A5_A0[4]),
    .in6(1'b0), .in7(1'b0), .out(out_3[5]), .sel(Shift_2_0));
  Multiplexer #(.select(3), .enable("false")) multiplexer_2 (
    .in0(A5_A0[4]), .in1(A5_A0[5]), .in2(A5_A0[0]), .in3(A5_A0[1]), .in4(A5_A0[2]), .in5(A5_A0[3]),
    .in6(1'b0), .in7(1'b0), .out(out_3[4]), .sel(Shift_2_0));
  Multiplexer #(.select(3), .enable("false")) multiplexer_3 (
    .in0(A5_A0[3]), .in1(A5_A0[4]), .in2(A5_A0[5]), .in3(A5_A0[0]), .in4(A5_A0[1]), .in5(A5_A0[2]),
    .in6(1'b0), .in7(1'b0), .out(out_3[3]), .sel(Shift_2_0));
  Multiplexer #(.select(3), .enable("false")) multiplexer_4 (
    .in0(A5_A0[2]), .in1(A5_A0[3]), .in2(A5_A0[4]), .in3(A5_A0[5]), .in4(A5_A0[0]), .in5(A5_A0[1]),
    .in6(1'b0), .in7(1'b0), .out(out_3[2]), .sel(Shift_2_0));
  Multiplexer #(.select(3), .enable("false")) multiplexer_5 (
    .in0(A5_A0[1]), .in1(A5_A0[2]), .in2(A5_A0[3]), .in3(A5_A0[4]), .in4(A5_A0[5]), .in5(A5_A0[0]),
    .in6(1'b0), .in7(1'b0), .out(out_3[1]), .sel(Shift_2_0));
  Multiplexer #(.select(3), .enable("false")) multiplexer_6 (
    .in0(A5_A0[0]), .in1(A5_A0[1]), .in2(A5_A0[2]), .in3(A5_A0[3]), .in4(A5_A0[4]), .in5(A5_A0[5]),
    .in6(1'b0), .in7(1'b0), .out(out_3[0]), .sel(Shift_2_0));

  // Other names for the same wires on the sheet: A0 = A5_A0[0]; A1 = A5_A0[1]; A2 = A5_A0[2]; A3 = A5_A0[3];
  //   A4 = A5_A0[4]; A5 = A5_A0[5]; R0 = out_3[0]; R1 = out_3[1]; R2 = out_3[2]; R3 = out_3[3]; R4 = out_3[4];
  //   R5 = out_3[5]
endmodule

module ALU (
  input  [5:0] A_5_0,
  input  [5:0] B_5_0,
  input  OP,
  output [5:0] out_4,
  output SF,
  output CF,
  output ZF
);

  wire or_1_out;
  wire [5:0] and_1_out_3, ror_1_out_3;

  AND and_1 (.A5_A0(A_5_0), .B5_B0(B_5_0), .out_3(and_1_out_3));
  ROR ror_1 (.A5_A0(A_5_0), .Shift_2_0(B_5_0[2:0]), .out_3(ror_1_out_3));
  Multiplexer #(.width(6), .enable("false")) multiplexer_1 (
    .in0(and_1_out_3), .in1(ror_1_out_3), .out(out_4), .sel(OP));
  or or_1 (or_1_out, out_4[0], out_4[1], out_4[2], out_4[3], out_4[4], out_4[5]);
  not not_1 (ZF, or_1_out);

  assign CF = 1'b0;
  assign SF = out_4[5];
endmodule

module _1_bit_register (
  input  Din,
  input  Sel,
  input  Clk,
  output Dout
);

  wire multiplexer_1_out;

  Multiplexer #(.enable("false")) multiplexer_1 (.in0(Dout), .in1(Din), .out(multiplexer_1_out), .sel(Sel));
  D_Flip_Flop d_ff_1 (.clk(Clk), .D(multiplexer_1_out), .Q(Dout));  // open: Qn, preset, en, reset
endmodule

module _6_bit_register (
  input  [5:0] Din_5_0,
  input  Dsel,
  input  Clk,
  output [5:0] out_4
);

  _1_bit_register u_1_bit_register_1 (.Din(Din_5_0[0]), .Sel(Dsel), .Clk(Clk), .Dout(out_4[0]));
  _1_bit_register u_1_bit_register_2 (.Din(Din_5_0[1]), .Sel(Dsel), .Clk(Clk), .Dout(out_4[1]));
  _1_bit_register u_1_bit_register_3 (.Din(Din_5_0[2]), .Sel(Dsel), .Clk(Clk), .Dout(out_4[2]));
  _1_bit_register u_1_bit_register_4 (.Din(Din_5_0[3]), .Sel(Dsel), .Clk(Clk), .Dout(out_4[3]));
  _1_bit_register u_1_bit_register_5 (.Din(Din_5_0[4]), .Sel(Dsel), .Clk(Clk), .Dout(out_4[4]));
  _1_bit_register u_1_bit_register_6 (.Din(Din_5_0[5]), .Sel(Dsel), .Clk(Clk), .Dout(out_4[5]));
endmodule

module _3_6_bit_register (
  input  Reg_en,
  input  [1:0] Wr,
  input  [5:0] Wrd,
  input  clk,
  input  [1:0] Ra,
  input  [1:0] Rb,
  output [5:0] out_7,
  output [5:0] out_8
);

  wire Reg0, Reg1, Reg2;
  wire [5:0] R0, R1, R2;

  Decoder #(.select(2)) decoder_1 (.out0(Reg0), .out1(Reg1), .out2(Reg2), .sel(Wr), .en(Reg_en));  // open: out3
  _6_bit_register u_6_bit_register_1 (.Din_5_0(Wrd), .Dsel(Reg0), .Clk(clk), .out_4(R0));
  _6_bit_register u_6_bit_register_2 (.Din_5_0(Wrd), .Dsel(Reg1), .Clk(clk), .out_4(R1));
  _6_bit_register u_6_bit_register_3 (.Din_5_0(Wrd), .Dsel(Reg2), .Clk(clk), .out_4(R2));
  Multiplexer #(.select(2), .width(6), .enable("false")) multiplexer_1 (
    .in0(R0), .in1(R1), .in2(R2), .out(out_7), .sel(Ra));  // open: in3
  Multiplexer #(.select(2), .width(6), .enable("false")) multiplexer_2 (
    .in0(R0), .in1(R1), .in2(R2), .out(out_8), .sel(Rb));  // open: in3
endmodule

module _1x1_SRAM (
  input  Read_Select_1,
  input  Read_Select_2,
  input  Write_Data,
  input  Write_Select,
  input  Clk,
  output Read_Data_1,
  output Read_Data_2
);

  wire d_ff_1_q, multiplexer_1_out;

  Multiplexer #(.enable("false")) multiplexer_1 (
    .in0(d_ff_1_q), .in1(Write_Data), .out(multiplexer_1_out), .sel(Write_Select));
  D_Flip_Flop d_ff_1 (.clk(Clk), .D(multiplexer_1_out), .Q(d_ff_1_q));  // open: Qn, preset, en, reset
  and and_1 (Read_Data_1, Read_Select_1, d_ff_1_q);
  and and_2 (Read_Data_2, Read_Select_2, d_ff_1_q);
endmodule

module _1x3_SRAM (
  input  Read_Select_1,
  input  Read_Select_2,
  input  Write_Select,
  input  [2:0] Write_Data,
  input  Clk,
  output [2:0] Read_Data_1,
  output [2:0] Read_Data_2
);

  _1x1_SRAM u_1x1_sram_1 (
    .Write_Data(Write_Data[0]), .Write_Select(Write_Select), .Clk(Clk), .Read_Data_1(Read_Data_1[0]),
    .Read_Data_2(Read_Data_2[0]), .Read_Select_1(Read_Select_1), .Read_Select_2(Read_Select_2));
  _1x1_SRAM u_1x1_sram_2 (
    .Write_Data(Write_Data[1]), .Write_Select(Write_Select), .Clk(Clk), .Read_Data_1(Read_Data_1[1]),
    .Read_Data_2(Read_Data_2[1]), .Read_Select_1(Read_Select_1), .Read_Select_2(Read_Select_2));
  _1x1_SRAM u_1x1_sram_3 (
    .Write_Data(Write_Data[2]), .Write_Select(Write_Select), .Clk(Clk), .Read_Data_1(Read_Data_1[2]),
    .Read_Data_2(Read_Data_2[2]), .Read_Select_1(Read_Select_1), .Read_Select_2(Read_Select_2));
endmodule

module _1x15_SRAM (
  input  Read_Select_1,
  input  Read_Select_2,
  input  Write_Select,
  input  Clk,
  input  [14:0] Write_data__14_0,
  output [14:0] Read_Data_1_14_0,
  output [14:0] Read_Data_2__14_0
);

  _1x3_SRAM u_1x3_sram_1 (
    .Read_Select_1(Read_Select_1), .Read_Select_2(Read_Select_2), .Write_Select(Write_Select),
    .Write_Data(Write_data__14_0[2:0]), .Clk(Clk), .Read_Data_1(Read_Data_1_14_0[2:0]),
    .Read_Data_2(Read_Data_2__14_0[2:0]));
  _1x3_SRAM u_1x3_sram_2 (
    .Read_Select_1(Read_Select_1), .Read_Select_2(Read_Select_2), .Write_Select(Write_Select),
    .Write_Data(Write_data__14_0[5:3]), .Clk(Clk), .Read_Data_1(Read_Data_1_14_0[5:3]),
    .Read_Data_2(Read_Data_2__14_0[5:3]));
  _1x3_SRAM u_1x3_sram_3 (
    .Read_Select_1(Read_Select_1), .Read_Select_2(Read_Select_2), .Write_Select(Write_Select),
    .Write_Data(Write_data__14_0[8:6]), .Clk(Clk), .Read_Data_1(Read_Data_1_14_0[8:6]),
    .Read_Data_2(Read_Data_2__14_0[8:6]));
  _1x3_SRAM u_1x3_sram_4 (
    .Read_Select_1(Read_Select_1), .Read_Select_2(Read_Select_2), .Write_Select(Write_Select),
    .Write_Data(Write_data__14_0[11:9]), .Clk(Clk), .Read_Data_1(Read_Data_1_14_0[11:9]),
    .Read_Data_2(Read_Data_2__14_0[11:9]));
  _1x3_SRAM u_1x3_sram_5 (
    .Read_Select_1(Read_Select_1), .Read_Select_2(Read_Select_2), .Write_Select(Write_Select),
    .Write_Data(Write_data__14_0[14:12]), .Clk(Clk), .Read_Data_1(Read_Data_1_14_0[14:12]),
    .Read_Data_2(Read_Data_2__14_0[14:12]));
endmodule

module _8x15_SRAM (
  input  [14:0] Write_Data,
  input  Write_Enable,
  input  [2:0] Write_Address_1_2_0,
  input  [2:0] Read_Address_1_2_0,
  input  [2:0] Read_Address_2_2_0,
  input  in_6,
  output [14:0] Read_data_1,
  output [14:0] Read_data_2
);

  wire R1_0, R1_1, R1_2, R1_3, R1_4, R1_5, R1_6, R1_7, R2_0, R2_1, R2_2, R2_3, R2_4, R2_5, R2_6, R2_7, W_0,
       W_1, W_2, W_3, W_4, W_5, W_6;
  wire [14:0] Rd1_0, Rd1_1, Rd1_2, Rd1_3, Rd1_4, Rd1_5, Rd1_6, Rd1_7, Rd2_0, Rd2_1, Rd2_2, Rd2_3, Rd2_4,
       Rd2_5, Rd2_6, Rd2_7;

  Decoder #(.select(3)) decoder_1 (
    .out0(W_0), .out1(W_1), .out2(W_2), .out3(W_3), .out4(W_4), .out5(W_5), .out6(W_6), .out7(R2_7),
    .sel(Write_Address_1_2_0), .en(Write_Enable));
  Decoder #(.select(3), .enable("false")) decoder_2 (
    .out0(R1_0), .out1(R1_1), .out2(R1_2), .out3(R1_3), .out4(R1_4), .out5(R1_5), .out6(R1_6), .out7(R1_7),
    .sel(Read_Address_1_2_0));
  Decoder #(.select(3), .enable("false")) decoder_3 (
    .out0(R2_0), .out1(R2_1), .out2(R2_2), .out3(R2_3), .out4(R2_4), .out5(R2_5), .out6(R2_6), .out7(R2_7),
    .sel(Read_Address_2_2_0));
  _1x15_SRAM u_1x15_sram_1 (
    .Read_Select_1(R1_0), .Read_Select_2(R2_0), .Write_Select(W_0), .Clk(in_6),
    .Write_data__14_0(Write_Data), .Read_Data_1_14_0(Rd1_0), .Read_Data_2__14_0(Rd2_0));
  _1x15_SRAM u_1x15_sram_2 (
    .Read_Select_1(R1_1), .Read_Select_2(R2_1), .Write_Select(W_1), .Clk(in_6),
    .Write_data__14_0(Write_Data), .Read_Data_1_14_0(Rd1_1), .Read_Data_2__14_0(Rd2_1));
  _1x15_SRAM u_1x15_sram_3 (
    .Read_Select_1(R1_2), .Read_Select_2(R2_2), .Write_Select(W_2), .Clk(in_6),
    .Write_data__14_0(Write_Data), .Read_Data_1_14_0(Rd1_2), .Read_Data_2__14_0(Rd2_2));
  _1x15_SRAM u_1x15_sram_4 (
    .Read_Select_1(R1_3), .Read_Select_2(R2_3), .Write_Select(W_3), .Clk(in_6),
    .Write_data__14_0(Write_Data), .Read_Data_1_14_0(Rd1_3), .Read_Data_2__14_0(Rd2_3));
  _1x15_SRAM u_1x15_sram_5 (
    .Read_Select_1(R1_4), .Read_Select_2(R2_4), .Write_Select(W_4), .Clk(in_6),
    .Write_data__14_0(Write_Data), .Read_Data_1_14_0(Rd1_4), .Read_Data_2__14_0(Rd2_4));
  _1x15_SRAM u_1x15_sram_6 (
    .Read_Select_1(R1_5), .Read_Select_2(R2_5), .Write_Select(W_5), .Clk(in_6),
    .Write_data__14_0(Write_Data), .Read_Data_1_14_0(Rd1_5), .Read_Data_2__14_0(Rd2_5));
  _1x15_SRAM u_1x15_sram_7 (
    .Read_Select_1(R1_6), .Read_Select_2(R2_6), .Write_Select(W_6), .Clk(in_6),
    .Write_data__14_0(Write_Data), .Read_Data_1_14_0(Rd1_6), .Read_Data_2__14_0(Rd2_6));
  _1x15_SRAM u_1x15_sram_8 (
    .Read_Select_1(R1_7), .Read_Select_2(R2_7), .Write_Select(R2_7), .Clk(in_6),
    .Write_data__14_0(Write_Data), .Read_Data_1_14_0(Rd1_7), .Read_Data_2__14_0(Rd2_7));
  assign Read_data_1 = Rd1_0 | Rd1_1 | Rd1_2 | Rd1_3 | Rd1_4 | Rd1_5 | Rd1_6 | Rd1_7;  // OR_Gate or_1, 15 bits wide
  assign Read_data_2 = Rd2_0 | Rd2_1 | Rd2_2 | Rd2_3 | Rd2_4 | Rd2_5 | Rd2_6 | Rd2_7;  // OR_Gate or_2, 15 bits wide

  // Other names for the same wires on the sheet: W_7 = R2_7
endmodule

module CPU (
  input  [2:0] in_1,
  input  [14:0] in_2,
  input  in_3,
  input  in_4,
  input  in_5
);

  wire alu_1_cf, alu_1_sf, alu_1_zf, CF, CPU_CLK, Imm_Sel, Jmp_Sel, Op, REG_EN, SF, ZF;
  wire [2:0] add_count_1_output_address__2_0, JG_Add, multiplexer_1_out, n8x15_sram_1_read_data_1_3, undriven;
  wire [3:0] n8x15_sram_1_read_data_1;
  wire [4:0] n8x15_sram_1_read_data_1_2;
  wire [5:0] alu_1_out_4, multiplexer_2_out, n3_6_bit_register_1_out_7, n3_6_bit_register_1_out_8;

  Multiplexer #(.width(3), .disabled(0), .enable("false")) multiplexer_1 (
    .in0(undriven), .in1(JG_Add), .out(multiplexer_1_out), .sel(Jmp_Sel));
  Add_count add_count_1 (.Input_Address__2_0(undriven), .Output_Address__2_0(add_count_1_output_address__2_0));
  program_counter program_counter_1 (
    .I__2_0(multiplexer_1_out), .Clock(CPU_CLK), .O__2_0(add_count_1_output_address__2_0));
  and and_1 (CPU_CLK, in_4, in_5);
  _8x15_SRAM u_8x15_sram_1 (
    .Write_Data(in_2), .Write_Enable(in_3), .Write_Address_1_2_0(in_1),
    .Read_Address_1_2_0(add_count_1_output_address__2_0), .in_6(in_4),
    .Read_data_1({n8x15_sram_1_read_data_1_3, JG_Add, n8x15_sram_1_read_data_1_2, n8x15_sram_1_read_data_1}));  // open: Read_Address_2_2_0, Read_data_2
  _3_6_bit_register u_3_6_bit_register_1 (
    .Reg_en(REG_EN), .Wrd(alu_1_out_4), .clk(CPU_CLK), .Ra(JG_Add[2:1]),
    .Rb({JG_Add[0], n8x15_sram_1_read_data_1_2[4]}), .out_7(n3_6_bit_register_1_out_7),
    .out_8(n3_6_bit_register_1_out_8));  // open: Wr
  Flag_register flag_register_1 (
    .CF(alu_1_cf), .Clock(CPU_CLK), .CF_2(CF), .SF_2(SF), .ZF_2(ZF), .SF(alu_1_sf), .ZF(alu_1_zf));
  Control_unit control_unit_1 (
    .Opcode_2_0(n8x15_sram_1_read_data_1_3), .ZF(ZF), .SF(SF), .op(Op), .Imm_sel(Imm_Sel), .WE(REG_EN),
    .JG(Jmp_Sel));
  Multiplexer #(.width(6), .disabled(0), .enable("false")) multiplexer_2 (
    .in0({JG_Add[0], n8x15_sram_1_read_data_1_2}), .in1(n3_6_bit_register_1_out_8), .out(multiplexer_2_out),
    .sel(Imm_Sel));
  ALU alu_1 (
    .A_5_0(n3_6_bit_register_1_out_7), .B_5_0(multiplexer_2_out), .OP(Op), .out_4(alu_1_out_4),
    .SF(alu_1_sf), .CF(alu_1_cf), .ZF(alu_1_zf));

  // Other names for the same wires on the sheet: CLK = in_4
endmodule

module program_counter (
  input  [2:0] I__2_0,
  input  Clock,
  output [2:0] O__2_0
);

  D_Flip_Flop d_ff_1 (.clk(Clock), .D(I__2_0[0]), .Q(O__2_0[0]));  // open: Qn, preset, en, reset
  D_Flip_Flop d_ff_2 (.clk(Clock), .D(I__2_0[1]), .Q(O__2_0[1]));  // open: Qn, preset, en, reset
  D_Flip_Flop d_ff_3 (.clk(Clock), .D(I__2_0[2]), .Q(O__2_0[2]));  // open: Qn, preset, en, reset
endmodule

module Flag_register (
  input  CF,
  input  SF,
  input  ZF,
  input  Clock,
  output CF_2,
  output SF_2,
  output ZF_2
);

  _1_bit_register u_1_bit_register_1 (.Din(CF), .Sel(1'b1), .Clk(Clock), .Dout(CF_2));
  _1_bit_register u_1_bit_register_2 (.Din(SF), .Sel(1'b1), .Clk(Clock), .Dout(SF_2));
  _1_bit_register u_1_bit_register_3 (.Din(ZF), .Sel(1'b1), .Clk(Clock), .Dout(ZF_2));
endmodule

module Add_count (
  input  [2:0] Input_Address__2_0,
  output [2:0] Output_Address__2_0
);

  wire [2:0] bit_extender_1_out;

  assign bit_extender_1_out = {{2{1'b0}}, 1'b1};  // Bit_Extender bit_extender_1
  Adder #(.width(3)) adder_1 (
    .a(Input_Address__2_0), .b(bit_extender_1_out), .out(Output_Address__2_0), .cin(1'b0));  // open: cout
endmodule

module Control_unit (
  input  [2:0] Opcode_2_0,
  input  ZF,
  input  SF,
  output op,
  output Imm_sel,
  output WE,
  output JG
);

  wire and_1_out, and_2_out, Brch_out, not_1_out, not_2_out, not_3_out, not_4_out, not_5_out, not_6_out,
       not_7_out;

  not not_1 (not_1_out, ZF);
  not not_2 (not_2_out, SF);
  and and_1 (and_1_out, not_1_out, not_2_out);
  not not_3 (not_3_out, Opcode_2_0[2]);
  not not_4 (not_4_out, Opcode_2_0[2]);
  not not_5 (not_5_out, Opcode_2_0[1]);
  not not_6 (not_6_out, Opcode_2_0[1]);
  not not_7 (not_7_out, Opcode_2_0[0]);
  and Imm (Imm_sel, not_3_out, Opcode_2_0[1]);
  and and_2 (and_2_out, not_4_out, not_5_out);
  and Brch (Brch_out, Opcode_2_0[2], not_6_out);
  or or_1 (WE, Imm_sel, and_2_out);
  and u_JG (JG, Brch_out, not_7_out, and_1_out);

  assign op = Opcode_2_0[0];
endmodule

module test_alu (
  input  [5:0] in_1,
  input  [5:0] in_2,
  input  in_3,
  output [5:0] out_4
);

  ALU alu_1 (.A_5_0(in_1), .B_5_0(in_2), .OP(in_3), .out_4(out_4));  // open: SF, CF, ZF
endmodule
